// Logisim project Misc.circ as structural Verilog: 4 circuits, main circuit HEX_DECODER
module HEX_DECODER (
  input  E,
  input  [3:0] BIN,
  output [8:0] L0,
  output [8:0] L1,
  output [8:0] L2,
  output [8:0] L3,
  output [8:0] L4
);

  PLA #(.in_width(5), .out_width(45), .\table ("0xxx1 110000011010000000000000000110000001110000000 # EXEMPLE\n0xxxx 000000000000000000000000000000000000000000000 # DISABLE\n10000 011111110100000001100010001100000001011111110 # 0\n10001 000000000000000000111111111010000000000000000 # 1\n10010 011000001100100001100010001100001101010000011 # 2\n10011 011101110100010001100010001100010001010000010 # 3\n10100 011111111000001000000001000111001000000111000 # 4\n10101 100011110100010001100010001100010001111110010 # 5\n10110 010001110100010001100010001100010001011111110 # 6\n10111 111000000100110000100001111100000000100000000 # 7\n11000 011101110100010001100010001100010001011101110 # 8\n11001 011111110100010001100010001100010001011100010 # 9\n11010 011111111100010000100010000100010000011111111 # A\n11011 011101110100010001100010001100010001111111111 # B\n11100 010000010100000001100000001100000001011111110 # C\n11101 011111110100000001100000001100000001111111111 # D\n11110 100000001100010001100010001100010001111111111 # E\n11111 100000000100010000100010000100010000111111111 # F")) pla_1 (
    .in({E, BIN}), .out({L4, L3, L2, L1, L0}));
  LED HEX_DEC_ENABLE (.in(E));
endmodule

module test (
  input  [15:0] A
);

  wire button_1_out, ENABLE_q;
  wire [8:0] hex_decoder_1_l0, hex_decoder_1_l1, hex_decoder_1_l2, hex_decoder_1_l3, hex_decoder_1_l4,
       hex_decoder_2_l0, hex_decoder_2_l1, hex_decoder_2_l2, hex_decoder_2_l3, hex_decoder_2_l4,
       hex_decoder_3_l0, hex_decoder_3_l1, hex_decoder_3_l2, hex_decoder_3_l3, hex_decoder_3_l4,
       hex_decoder_4_l0, hex_decoder_4_l1, hex_decoder_4_l2, hex_decoder_4_l3, hex_decoder_4_l4;

  DotMatrix #(.matrixrows(9)) dotmatrix_1 (
    .col0(hex_decoder_1_l0), .col1(hex_decoder_1_l1), .col2(hex_decoder_1_l2), .col3(hex_decoder_1_l3),
    .col4(hex_decoder_1_l4));
  DotMatrix #(.matrixrows(9)) dotmatrix_2 (
    .col0(hex_decoder_2_l0), .col1(hex_decoder_2_l1), .col2(hex_decoder_2_l2), .col3(hex_decoder_2_l3),
    .col4(hex_decoder_2_l4));
  HEX_DECODER hex_decoder_1 (
    .BIN(A[15:12]), .E(ENABLE_q), .L3(hex_decoder_1_l3), .L4(hex_decoder_1_l4), .L0(hex_decoder_1_l0),
    .L1(hex_decoder_1_l1), .L2(hex_decoder_1_l2));
  HEX_DECODER hex_decoder_2 (
    .BIN(A[11:8]), .E(ENABLE_q), .L3(hex_decoder_2_l3), .L4(hex_decoder_2_l4), .L0(hex_decoder_2_l0),
    .L1(hex_decoder_2_l1), .L2(hex_decoder_2_l2));
  T_Flip_Flop ENABLE (.clk(button_1_out), .T(button_1_out), .Q(ENABLE_q));  // open: Qn, preset, reset
  Button button_1 (.out(button_1_out));
  LED led_1 (.in(ENABLE_q));
  DotMatrix #(.matrixrows(9)) dotmatrix_3 (
    .col0(hex_decoder_3_l0), .col1(hex_decoder_3_l1), .col2(hex_decoder_3_l2), .col3(hex_decoder_3_l3),
    .col4(hex_decoder_3_l4));
  DotMatrix #(.matrixrows(9)) dotmatrix_4 (
    .col0(hex_decoder_4_l0), .col1(hex_decoder_4_l1), .col2(hex_decoder_4_l2), .col3(hex_decoder_4_l3),
    .col4(hex_decoder_4_l4));
  HEX_DECODER hex_decoder_3 (
    .BIN(A[7:4]), .E(ENABLE_q), .L3(hex_decoder_3_l3), .L4(hex_decoder_3_l4), .L0(hex_decoder_3_l0),
    .L1(hex_decoder_3_l1), .L2(hex_decoder_3_l2));
  HEX_DECODER hex_decoder_4 (
    .BIN(A[3:0]), .E(ENABLE_q), .L3(hex_decoder_4_l3), .L4(hex_decoder_4_l4), .L0(hex_decoder_4_l0),
    .L1(hex_decoder_4_l1), .L2(hex_decoder_4_l2));
  // Probe on A
endmodule

module SHIFT_ADD (
  input  in_1,
  input  in_2,
  input  in_3,
  input  in_4
);
endmodule

module HEX_DISP (
  input  [15:0] A
);

  Hex_Digit_Display #(.decimalPoint("false")) hex_digit_display_1 (.value(A[15:12]));
  Hex_Digit_Display #(.decimalPoint("false")) hex_digit_display_2 (.value(A[11:8]));
  Hex_Digit_Display #(.decimalPoint("false")) hex_digit_display_3 (.value(A[7:4]));
  Hex_Digit_Display #(.decimalPoint("false")) hex_digit_display_4 (.value(A[3:0]));
endmodule
